# Fritzing sketch amplifier_mqtt (saved by Fritzing 0.9.4)

parts:
  WeMos_D1_Mini1 = WeMos D1 Mini
  HLK-PM1 = HLK-PM12 [part_number=HLK-PM12]
  Factory_power_switch = Pushbutton [package="[THT]"]
  Factory_AC_power = Power plug
  Relay_module = WeMos D1 Mini Relay Shield
  ACS712 = ACS712 Low Current Sensor Board v12
  R1 = Resistor [tolerance=±5% resistance=220 package=THT]
  R2 = Resistor [tolerance=±5% resistance=220 package="1206 [SMD]"]

nets:
  5V: WeMos_D1_Mini1.5V, HLK-PM1.+Vo, Relay_module.5V, ACS712.5V
  N1: WeMos_D1_Mini1.A0, R1.Pin_1, R2.Pin_0
  N2: WeMos_D1_Mini1.D1, Relay_module.D1
  N3: WeMos_D1_Mini1.G, HLK-PM1.-Vo, Relay_module.G, ACS712.GND, R2.Pin_1
  N4: HLK-PM1.AC_1, Factory_AC_power.VCC
  N5: HLK-PM1.AC_2, Factory_AC_power.GND
  N6: Factory_power_switch.Pin_1, Relay_module.COM
  N7: Factory_power_switch.Pin_3, Relay_module.NO
  N8: ACS712.VO, R1.Pin_0

notes:
  10K
  2.2K
  29V DC line  from factory board
