# Fritzing sketch humidifier_mqtt (saved by Fritzing 0.9.4)

parts:
  WeMos_D1_Mini1 = WeMos D1 Mini
  12V = female pin header, 2 pins [form="♀ (female)"]
  12V_to_5V_converter = RioRand LM2596
  Humidifier_factory_switch = Toggle Switch [package=THT]
  R1 = Resistor [tolerance=±5% resistance=220 package=THT]
  Relay_module = G3VM-61E1 [package=g3vm-61e1]

nets:
  N1: WeMos_D1_Mini1.3V3, Humidifier_factory_switch.COM
  N2: WeMos_D1_Mini1.5V, 12V_to_5V_converter.Pin_3, Relay_module.P$2
  N3: WeMos_D1_Mini1.D1, Relay_module.P$1
  N4: WeMos_D1_Mini1.D5, Humidifier_factory_switch.L2, R1.Pin_1
  N5: WeMos_D1_Mini1.G, 12V_to_5V_converter.Pin_4, R1.Pin_0, Relay_module.P$3
  N6: 12V.pin1, 12V_to_5V_converter.Pin_1
  N7: 12V.pin2, 12V_to_5V_converter.Pin_2

notes:
  10K resistor
  from factory board
  Factory ultrasonic transducer power
